# Fritzing sketch automaticGreenhouseCircuit (saved by Fritzing 0.9.9b)
breadboards: 1

parts:
  J1 = STM32 Nucleo boards
  KY-1 = Keyes Relay [package=THT]
  DHT1 = DHT11 Humitidy and Temperature Sensor (3 pins)
  J2 = Basic Servo
  Capacitive_Soil_Moisture_Sensor1 = DFRobot Capacitive Soil Moisture Sensor V1.0 [part_number=SEN0193]

nets:
  N1: J1.A0, Capacitive_Soil_Moisture_Sensor1.A
  N2: J1.A1, DHT1.DATA
  N3: J1.D2, KY-1.signal
  VCC: J1.5V, KY-1.power, DHT1.VDD, J2.vcc, Capacitive_Soil_Moisture_Sensor1.VCC
  GND: J1.GND, KY-1.ground, DHT1.GND, J2.gnd, Capacitive_Soil_Moisture_Sensor1.GND
  N4: J1.PA15, J2.pulse

custom parts:
  Keyes Relay: The Keyes 5V relay module is suitable for SCM development, home appliance control. It uses a 5V~12V TIL control signal which can control DC / AC signal.
  DHT11 Humitidy and Temperature Sensor (3 pins): DHT11 Humidity and Temperature Sensor (3 pins) from the design created by John De Cristofaro for Adafruit Industries.
  DFRobot Capacitive Soil Moisture Sensor V1.0: DFRobot Capacitive Soil Moisture Sensor V1.0 This product measures soil moisture levels by capacitive sensing, rather than resistive sensing like other types of moisture sensor. It is made of a corrosion resistant material giving it a long service life. Insert it into soil and impress your friends with the real-time soil moisture data! The product includes an on-board voltage regulator which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
